# Fritzing sketch circuito 2 (saved by Fritzing 0.9.3b)

parts:
  Part1 = FC-28 Soil Hygrometer Module
  Part2 = FC-28 Soil Hygrometer Module - Probe
  Raspberry_Pi_1 = Raspberry Pi 3 [part_number=RPI-3-V1.2]
  S1 = Tilt Switch [package=THT]
  KY-1 = Keyes Relay [package=THT]
  Part3 = Arduino Mega 2560 (Rev3)
  J1 = Piezo Speaker
  S2 = Pushbutton [package="[THT]"]
  R1 = Resistor [tolerance=±5% resistance=100 package=THT]
  R2 = Resistor [tolerance=±5% resistance=220 package=THT]
  R3 = Resistor [tolerance=±5% resistance=220 package=THT]
  R4 = Photocell (LDR) [package=THT]
  C2 = Electrolytic Capacitor [capacitance=1µF package="100 mil [THT, electrolytic]"]

nets:
  VCC: Part1.VCC, KY-1.power, Part3.5V
  GND: Part1.GND, KY-1.ground, Part3.GND, J1.pin1, R2.Pin_0, R3.Pin_0
  N1: Part1.AO, Part3.A8
  N2: Part1.POS, Part2.POS
  N3: Part1.NEG, Part2.NEG
  N4: Raspberry_Pi_1.3v3, R4.pin_1
  N5: Raspberry_Pi_1.GIPO23, R4.pin_0, C2.+
  N6: Raspberry_Pi_1.GND, C2.-
  N7: S1.Pin_1, S2.Pin_3, S2.Pin_4
  N8: S1.Pin_2, Part3.D11_PWM, R3.Pin_1
  N9: KY-1.signal, Part3.D8_PWM
  N10: Part3.D10_PWM, R1.Pin_1
  N11: Part3.D2_PWM, S2.Pin_1, S2.Pin_2, R2.Pin_1
  N12: J1.pin2, R1.Pin_0

custom parts:
  FC-28 Soil Hygrometer Module: The FC-28 is a soil hygrometer module that uses the Texas Instruments LM393 comparator chip to provide an analog measurement of soil humidity. The digital output is high when soil moisture is over a certain threshold, as determined by adjusting the potentiometer.
  FC-28 Soil Hygrometer Module - Probe: The FC-28 is a soil hygrometer module that uses the Texas Instruments LM393 comparator chip to provide an analog measurement of soil humidity.
  Keyes Relay: The Keyes 5V relay module is suitable for SCM development, home appliance control. It uses a 5V~12V TIL control signal which can control DC / AC signal.
